# Fritzing sketch display (saved by Fritzing 0.9.3b)
perfboards: 1

parts:
  Round = male pin header, 7 pins [form="♂ (male)"]
  Square = male pin header, 8 pins [form="♂ (male)"]
  USB = female pin header, 9 pins [form="♀ (female)"]

nets:
  RST: Round.pin1, Square.pin3, USB.pin2
  CS_R: Round.pin2, USB.pin3
  DC: Round.pin3, Square.pin2, USB.pin4
  SDA: Round.pin4, Square.pin4, USB.pin5
  SCL: Round.pin5, Square.pin5, USB.pin6
  GND: Round.pin6, Square.pin7, USB.pin7
  5V: Round.pin7, Square.pin6, USB.pin8
  CS_S: Square.pin1, USB.pin1
  3.3V: Square.pin8, USB.pin9

notes:
  Square
  Round
  USB
