# Fritzing sketch main (saved by Fritzing 0.9.3b)
circuit board: 7cm x 3cm
perfboards: 1

parts:
  ESP32_Mini_D1 = MH-ET Live Minikit for ESP32
  SIM808 = female pin header, 7 pins [form="♀ (female)"]
  LCD = female pin header, 8 pins [form="♀ (female)"]
  POWERIN = Screw terminal - 2 pins [package=THT]

nets:
  RST: ESP32_Mini_D1.RST, LCD.pin8
  GPRS_PIN_RX: ESP32_Mini_D1.IO26, SIM808.pin3
  SCL: ESP32_Mini_D1.IO18, LCD.pin7
  GPRS_PIN_TX: ESP32_Mini_D1.IO19, SIM808.pin2
  SDA: ESP32_Mini_D1.IO23, LCD.pin1
  CS_R: ESP32_Mini_D1.IO22, LCD.pin6
  DC: ESP32_Mini_D1.IO21, LCD.pin5
  CS_S: ESP32_Mini_D1.IO17, LCD.pin4
  GND: ESP32_Mini_D1.GND, SIM808.pin6, LCD.pin3, POWERIN.pin1
  5V: ESP32_Mini_D1.VCC, SIM808.pin5, LCD.pin2, POWERIN.pin2

custom parts:
  MH-ET Live Minikit for ESP32: MH-ET Live Minikit for ESP32 ( http://mh.nodebb.com/topic/8/mh-et-live-minikit-for-esp32/2/) PCB footprint is invalid.
