# Fritzing sketch main_v1 (saved by Fritzing 1.0.0rc)
circuit board: 11.0338cm x 3.58782cm
perfboards: 2

parts:
  M1 = NEO-6M GPS Module [part_number=GY-GPS6MV2]
  A1 = lolin S3 mini
  SquareLCD = female pin header, 8 pins [form="♀ (female)"]
  RoundLCD1 = female pin header, 7 pins [form="♀ (female)"]

nets:
  GND: M1.GND, A1.Pin_18, A1.Pin_26, SquareLCD.pin1, RoundLCD1.pin2
  TX: M1.Tx, A1.Pin_3
  RX: M1.Rx, A1.Pin_2
  5V: M1.Vcc, A1.Pin_25, SquareLCD.pin2, RoundLCD1.pin1
  SCL: A1.Pin_4, SquareLCD.pin3, RoundLCD1.pin3
  SDA: A1.Pin_6, SquareLCD.pin4, RoundLCD1.pin4
  CS_S: A1.Pin_7, SquareLCD.pin7
  3.3V: A1.Pin_8, SquareLCD.pin8
  DC: A1.Pin_28, SquareLCD.pin6, RoundLCD1.pin5
  CS_R: A1.Pin_29, RoundLCD1.pin6
  RST: A1.Pin_30, SquareLCD.pin5, RoundLCD1.pin7

custom parts:
  NEO-6M GPS Module: GY-GPS6MV2 NEO-6M GPS Module Module based on U-blox NEO-6M GPS engine, incorporating regulator for 3.3-5V DC input, MS621FE-compatible rechargeable battery for backup and EEPROM for storing configuration settings. Links: NEO-6 series product information page NEO-6 Datasheet
  lolin S3 mini: WiFi + Bluetooth 5 (LE) boards based ESP32-S3FH4R2.
