# Fritzing sketch main_v2 (saved by Fritzing 0.9.3b)
perfboards: 1

parts:
  ESP32_Mini_D1 = MH-ET Live Minikit for ESP32
  SIM808 = female pin header, 7 pins [form="♀ (female)"]
  POWERIN = screw terminal, 2 pins
  LCD = female pin header, 10 pins [form="♀ (female)"]

nets:
  GND: ESP32_Mini_D1.GND, SIM808.pin6, POWERIN.pin1, LCD.pin4
  RST: ESP32_Mini_D1.RST, LCD.pin10
  GPRS_PIN_RX: ESP32_Mini_D1.IO26, SIM808.pin3
  SCL: ESP32_Mini_D1.IO18, LCD.pin9
  GPRS_PIN_TX: ESP32_Mini_D1.IO19, SIM808.pin2
  SDA: ESP32_Mini_D1.IO23, LCD.pin2
  3.3V: ESP32_Mini_D1.3.3V, LCD.pin1
  CS_R: ESP32_Mini_D1.IO22, LCD.pin8
  DC: ESP32_Mini_D1.IO21, LCD.pin7
  CS_S: ESP32_Mini_D1.IO17, LCD.pin6
  5V: ESP32_Mini_D1.VCC, SIM808.pin5, POWERIN.pin2, LCD.pin3

custom parts:
  MH-ET Live Minikit for ESP32: MH-ET Live Minikit for ESP32 ( http://mh.nodebb.com/topic/8/mh-et-live-minikit-for-esp32/2/) PCB footprint is invalid.
